// Logisim project Basic Computer.circ as structural Verilog: 23 circuits, main circuit Main
module Main (
  input  [7:0] INPR
);

  wire alu_1_e_out, Clock, clock_1_out, Comp, E, e_controler_1_clear, e_controler_1_d_2, FGI,
       fgi_o_ien_controler_1_clock_2, fgi_o_ien_controler_1_clock_3, fgi_o_ien_controler_1_clock_4,
       fgi_o_ien_controler_1_fgi_j, fgi_o_ien_controler_1_fgi_k, fgi_o_ien_controler_1_fgo_j,
       fgi_o_ien_controler_1_fgo_k, fgi_o_ien_controler_1_ien_j, fgi_o_ien_controler_1_ien_k, FGO, HLT, I,
       IEN, memory_controler_1_mr_load, not_1_out, p, pc_controler_1_clear, pc_controler_1_inc,
       pc_controler_1_load, R, r_t;
  wire [2:0] BUS_Selector;
  wire [3:0] outr_1_out_5, outr_1_out_6;
  wire [7:0] D;
  wire [11:0] B;
  wire [15:0] AC, alu_1_out, AR, BUS_IN, DR, IR, MR, PC, ram_1_data, T, TR;

  BUS_Selector bus_selector_1 (.D(D), .T(T), .B(B), .R(R), .I(I), .p(p), .Bus_Select(BUS_Selector));
  Clock clock_1 (.out(clock_1_out));
  and and_1 (r_t, D[7], ~I, T[3]);  // AND_Gate
  SC sc_1 (.R(R), .I(I), .T_2(T), .T(T), .D(D), .Clock(Clock));
  and and_2 (Clock, clock_1_out, ~HLT);  // AND_Gate
  and and_3 (p, D[7], I, T[3]);
  FGI fgi_1 (
    .FGI_J(fgi_o_ien_controler_1_fgi_j), .Clock(fgi_o_ien_controler_1_clock_2),
    .FGI_K(fgi_o_ien_controler_1_fgi_k), .FGI_OUT(FGI));
  FGI_O_IEN_Controler fgi_o_ien_controler_1 (
    .p(p), .R(R), .INPR(INPR), .FGI_K(fgi_o_ien_controler_1_fgi_k), .FGI_J(fgi_o_ien_controler_1_fgi_j),
    .FGO_K(fgi_o_ien_controler_1_fgo_k), .FGO_J(fgi_o_ien_controler_1_fgo_j),
    .IEN_K(fgi_o_ien_controler_1_ien_k), .IEN_J(fgi_o_ien_controler_1_ien_j), .T(T), .B(B), .Clock(Clock),
    .Clock_2(fgi_o_ien_controler_1_clock_2), .Clock_3(fgi_o_ien_controler_1_clock_3),
    .Clock_4(fgi_o_ien_controler_1_clock_4));
  FGO fgo_1 (
    .FGO_J(fgi_o_ien_controler_1_fgo_j), .Clock(fgi_o_ien_controler_1_clock_3),
    .FGO_K(fgi_o_ien_controler_1_fgo_k), .FGO_OUT(FGO));
  IEN ien_1 (
    .IEN_J(fgi_o_ien_controler_1_ien_j), .Clock(fgi_o_ien_controler_1_clock_4),
    .IEN_K(fgi_o_ien_controler_1_ien_k), .IEN_OUT(IEN));
  R r_1 (.T(T), .FGO(FGO), .IEN(IEN), .FGI(FGI), .OUT(R), .Clock(Clock));
  AR ar_1 (.BUS_IN(BUS_IN), .I(I), .Clock(Clock), .T(T), .D(D), .BUS_OUT(AR), .R(R));
  IR ir_1 (.T(T), .B(B), .I(I), .D(D), .BUS_OUT(IR), .HLT(HLT), .Clock(Clock), .R(R), .Bus_IN(BUS_IN));
  PC pc_1 (
    .Bus_IN(BUS_IN), .Bus_OUT(PC), .Clear(pc_controler_1_clear), .Clock(Clock), .Inc(pc_controler_1_inc),
    .Load(pc_controler_1_load));
  TR tr_1 (.Bus_IN(BUS_IN), .T(T), .R(R), .Bus_OUT(TR), .Clock(Clock));
  DR dr_1 (.Bus_IN(BUS_IN), .D(D), .T(T), .Clock(Clock), .Bus_OUT(DR));
  OUTR outr_1 (.Bus_IN(BUS_IN), .P(p), .B(B), .out_5(outr_1_out_5), .out_6(outr_1_out_6), .Clock(Clock));
  PC_Controler pc_controler_1 (
    .R_2(R), .E(E), .FGO(FGO), .FGI(FGI), .Load(pc_controler_1_load), .Clear(pc_controler_1_clear),
    .INC(pc_controler_1_inc), .DR(DR), .AC(AC), .B(B), .D(D), .r(r_t), .T(T), .p(p));
  Hex_Digit_Display hex_digit_display_1 (.value(outr_1_out_5));  // open: dp
  Multiplexer #(.select(3), .width(16), .enable("false")) multiplexer_1 (
    .in1(AR), .in2(PC), .in3(DR), .in4(AC), .in5(IR), .in6(TR), .in7(MR), .out(BUS_IN), .sel(BUS_Selector));  // open: in0
  Hex_Digit_Display hex_digit_display_2 (.value(outr_1_out_6));  // open: dp
  ALU alu_1 (
    .r(r_t), .E(E), .p(p), .E_OUT(alu_1_e_out), .AC(AC), .DR(DR), .INPR(INPR), .D(D), .T(T), .B(B),
    .OUT(alu_1_out));
  Memory_Controler memory_controler_1 (.MR_Load(memory_controler_1_mr_load), .D(D), .T(T), .R(R));
  E_Controler e_controler_1 (
    .r(r_t), .IN(alu_1_e_out), .Comp(Comp), .D_2(e_controler_1_d_2), .Clear(e_controler_1_clear), .T(T),
    .B(B), .D(D));
  AC ac_1 (.ALU_IN(alu_1_out), .r(r_t), .B(B), .Clock(Clock), .Bus_OUT(AC));
  not not_1 (not_1_out, memory_controler_1_mr_load);
  RAM #(.addrWidth(12), .dataWidth(16)) ram_1 (
    .addr(AR[11:0]), .data(ram_1_data), .clk(Clock), .ld(memory_controler_1_mr_load));  // open: sel, clr
  E e_1 (.Out(E), .Clock(Clock), .D(e_controler_1_d_2), .Comp(Comp), .Clear(e_controler_1_clear));
  assign MR = memory_controler_1_mr_load ? ram_1_data : 16'bz;  // Controlled_Buffer controlled_buffer_1
  assign ram_1_data = not_1_out ? BUS_IN : 16'bz;  // Controlled_Buffer controlled_buffer_2

  // Other names for the same wires on the sheet: INRP[7:0] = INPR
endmodule

module AR (
  input  R,
  input  [15:0] T,
  input  [7:0] D,
  input  [15:0] BUS_IN,
  input  I,
  input  Clock,
  output [15:0] BUS_OUT
);

  wire and_1_out, and_2_out, and_3_out, and_4_out, and_5_out, or_1_out, or_2_out;
  wire [11:0] adder_1_out, multiplexer_1_out;

  and and_1 (and_1_out, ~D[7], I, T[3]);  // AND_Gate
  and and_2 (and_2_out, T[2], ~R);  // AND_Gate
  and and_3 (and_3_out, ~R, T[0]);  // AND_Gate
  and and_4 (and_4_out, D[5], T[4]);
  or or_1 (or_1_out, and_1_out, and_2_out, and_3_out);
  Multiplexer #(.width(12), .enable("false")) multiplexer_1 (
    .in0(BUS_IN[11:0]), .in1(adder_1_out), .out(multiplexer_1_out), .sel(and_4_out));
  or or_2 (or_2_out, and_4_out, or_1_out);
  Register #(.width(12)) AR (.D(multiplexer_1_out), .en(or_2_out), .Q(BUS_OUT[11:0]), .clk(Clock), .clr(and_5_out));
  and and_5 (and_5_out, R, T[0]);
  Adder #(.width(12)) adder_1 (.a(12'h1), .b(BUS_OUT[11:0]), .out(adder_1_out));  // open: cin, cout

  assign BUS_OUT[15:12] = 4'b0000;
endmodule

module Full_Adder (
  input  Ci,
  input  Ai,
  input  Bi,
  output Si,
  output Ci_1
);

  wire half_adder_1_c, half_adder_1_s, half_adder_2_c;

  Half_Adder half_adder_1 (.A(Ai), .B(Bi), .S(half_adder_1_s), .C(half_adder_1_c));
  Half_Adder half_adder_2 (.A(Ci), .B(half_adder_1_s), .S(Si), .C(half_adder_2_c));
  or or_1 (Ci_1, half_adder_2_c, half_adder_1_c);
endmodule

module Adder_16 (
  input  [15:0] A,
  input  [15:0] B,
  input  Cin,
  output [15:0] S,
  output Cout
);

  wire full_adder_2_ci_1, full_adder_3_ci_1, full_adder_4_ci_1, full_adder_5_ci_1, full_adder_6_ci_1,
       full_adder_7_ci_1, full_adder_8_ci_1, full_adder_9_ci_1, full_adder_10_ci_1, full_adder_11_ci_1,
       full_adder_12_ci_1, full_adder_13_ci_1, full_adder_14_ci_1, full_adder_15_ci_1, full_adder_16_ci_1;

  Full_Adder full_adder_1 (.Ci(full_adder_2_ci_1), .Ai(A[15]), .Bi(B[15]), .Si(S[15]), .Ci_1(Cout));
  Full_Adder full_adder_2 (.Ci(full_adder_3_ci_1), .Ai(A[14]), .Bi(B[14]), .Si(S[14]), .Ci_1(full_adder_2_ci_1));
  Full_Adder full_adder_3 (.Ci(full_adder_4_ci_1), .Ai(A[13]), .Bi(B[13]), .Si(S[13]), .Ci_1(full_adder_3_ci_1));
  Full_Adder full_adder_4 (.Ci(full_adder_5_ci_1), .Ai(A[12]), .Bi(B[12]), .Si(S[12]), .Ci_1(full_adder_4_ci_1));
  Full_Adder full_adder_5 (.Ci(full_adder_6_ci_1), .Ai(A[11]), .Bi(B[11]), .Si(S[11]), .Ci_1(full_adder_5_ci_1));
  Full_Adder full_adder_6 (.Ci(full_adder_7_ci_1), .Ai(A[10]), .Bi(B[10]), .Si(S[10]), .Ci_1(full_adder_6_ci_1));
  Full_Adder full_adder_7 (.Ci(full_adder_8_ci_1), .Ai(A[9]), .Bi(B[9]), .Si(S[9]), .Ci_1(full_adder_7_ci_1));
  Full_Adder full_adder_8 (.Ci(full_adder_9_ci_1), .Ai(A[8]), .Bi(B[8]), .Si(S[8]), .Ci_1(full_adder_8_ci_1));
  Full_Adder full_adder_9 (.Ci(full_adder_10_ci_1), .Ai(A[7]), .Bi(B[7]), .Si(S[7]), .Ci_1(full_adder_9_ci_1));
  Full_Adder full_adder_10 (.Ci(full_adder_11_ci_1), .Ai(A[6]), .Bi(B[6]), .Si(S[6]), .Ci_1(full_adder_10_ci_1));
  Full_Adder full_adder_11 (.Ci(full_adder_12_ci_1), .Ai(A[5]), .Bi(B[5]), .Si(S[5]), .Ci_1(full_adder_11_ci_1));
  Full_Adder full_adder_12 (.Ci(full_adder_13_ci_1), .Ai(A[4]), .Bi(B[4]), .Si(S[4]), .Ci_1(full_adder_12_ci_1));
  Full_Adder full_adder_13 (.Ci(full_adder_14_ci_1), .Ai(A[3]), .Bi(B[3]), .Si(S[3]), .Ci_1(full_adder_13_ci_1));
  Full_Adder full_adder_14 (.Ci(full_adder_15_ci_1), .Ai(A[2]), .Bi(B[2]), .Si(S[2]), .Ci_1(full_adder_14_ci_1));
  Full_Adder full_adder_15 (.Ci(full_adder_16_ci_1), .Ai(A[1]), .Bi(B[1]), .Si(S[1]), .Ci_1(full_adder_15_ci_1));
  Full_Adder full_adder_16 (.Ci(Cin), .Ai(A[0]), .Bi(B[0]), .Si(S[0]), .Ci_1(full_adder_16_ci_1));
endmodule

module Half_Adder (
  input  A,
  input  B,
  output S,
  output C
);

  xor xor_1 (S, A, B);
  and and_1 (C, A, B);
endmodule

module IR (
  input  [15:0] Bus_IN,
  input  [15:0] T,
  input  R,
  input  Clock,
  output [11:0] B,
  output I,
  output [7:0] D,
  output [15:0] BUS_OUT,
  output HLT
);

  wire and_1_out;

  and and_1 (and_1_out, ~R, T[1]);  // AND_Gate
  Register #(.width(16)) register_1 (.D(Bus_IN), .en(and_1_out), .Q({BUS_OUT[15:12], B}), .clk(Clock));  // open: clr
  and and_2 (HLT, B[0], ~B[1], ~B[2], ~B[3], ~B[4], ~B[5], ~B[6], ~B[7], ~B[8], ~B[9], ~B[10], ~B[11], BUS_OUT[12], BUS_OUT[13], BUS_OUT[14], ~BUS_OUT[15]);  // AND_Gate
  Decoder #(.select(3), .enable("false")) decoder_1 (
    .out0(D[0]), .out1(D[1]), .out2(D[2]), .out3(D[3]), .out4(D[4]), .out5(D[5]), .out6(D[6]), .out7(D[7]),
    .sel(BUS_OUT[14:12]));

  assign BUS_OUT[11:0] = B;
  assign I = BUS_OUT[15];
endmodule

module PC (
  input  [15:0] Bus_IN,
  input  Clock,
  input  Load,
  input  Clear,
  input  Inc,
  output [15:0] Bus_OUT
);

  wire or_1_out;
  wire [11:0] adder_1_out, multiplexer_1_out;

  Multiplexer #(.width(12)) multiplexer_1 (
    .in0(Bus_IN[11:0]), .in1(adder_1_out), .out(multiplexer_1_out), .sel(Inc));  // open: en
  or or_1 (or_1_out, Inc, Load);
  Register #(.width(12)) register_1 (.D(multiplexer_1_out), .en(or_1_out), .Q(Bus_OUT[11:0]), .clk(Clock), .clr(Clear));
  Adder #(.width(12)) adder_1 (.a(12'h1), .b(Bus_OUT[11:0]), .out(adder_1_out));  // open: cin, cout

  assign Bus_OUT[15:12] = 4'b0000;
endmodule

module PC_Controler (
  input  [7:0] D,
  input  [15:0] DR,
  input  [15:0] AC,
  input  [11:0] B,
  input  r,
  input  p,
  input  R_2,
  input  [15:0] T,
  input  E,
  input  FGO,
  input  FGI,
  output Load,
  output Clear,
  output INC
);

  wire AC_All, and_1_out, and_2_out, and_3_out, and_4_out, and_5_out, and_6_out, and_7_out, and_8_out,
       and_9_out, and_10_out, and_11_out, DR_All, T6;

  or or_1 (DR_All, DR[15], DR[14], DR[13], DR[12], DR[11], DR[10], DR[9], DR[8], DR[7], DR[6], DR[5], DR[4], DR[3], DR[2], DR[1], DR[0]);
  or or_2 (AC_All, AC[15], AC[14], AC[13], AC[12], AC[11], AC[10], AC[9], AC[8], AC[7], AC[6], AC[5], AC[4], AC[3], AC[2], AC[1], AC[0]);
  and and_1 (and_1_out, D[5], T[5]);
  and and_2 (and_2_out, B[2], r, ~AC_All);  // AND_Gate
  and and_3 (and_3_out, AC[15], r, B[3]);
  and and_4 (and_4_out, T6, D[6], ~DR_All);  // AND_Gate
  and and_5 (and_5_out, r, B[1], ~E);  // AND_Gate
  and and_6 (and_6_out, D[4], T[4]);
  and and_7 (and_7_out, ~R_2, T[1]);  // AND_Gate
  and and_8 (and_8_out, R_2, T[2]);
  and and_9 (and_9_out, B[4], r, ~AC[15]);  // AND_Gate
  and and_10 (and_10_out, p, B[8], FGO);
  and and_11 (and_11_out, p, B[9], FGI);
  or or_3 (Load, and_6_out, and_1_out);
  and and_12 (Clear, R_2, T[1]);
  or or_4 (INC, and_7_out, and_8_out, and_9_out, and_2_out, and_3_out, and_4_out, and_5_out, and_10_out, and_11_out);

  // Other names for the same wires on the sheet: R_t = R_2
endmodule

module TR (
  input  [15:0] Bus_IN,
  input  [15:0] T,
  input  R,
  input  Clock,
  output [15:0] Bus_OUT
);

  wire and_1_out;
  wire [15:0] adder_1_out, multiplexer_1_out;

  and and_1 (and_1_out, T[0], R);
  Multiplexer #(.width(16)) multiplexer_1 (
    .in0(Bus_IN), .in1(adder_1_out), .out(multiplexer_1_out), .sel(and_1_out));  // open: en
  Register #(.width(16)) TR (.D(multiplexer_1_out), .en(and_1_out), .Q(Bus_OUT), .clk(Clock));  // open: clr
  Adder #(.width(16)) adder_1 (.a(16'h1), .b(Bus_OUT), .out(adder_1_out));  // open: cin, cout
endmodule

module DR (
  input  [7:0] D,
  input  [15:0] T,
  input  [15:0] Bus_IN,
  input  Clock,
  output [15:0] Bus_OUT
);

  wire and_1_out, and_2_out, or_1_out, or_2_out;
  wire [15:0] adder_1_out, multiplexer_1_out;

  or or_1 (or_1_out, D[0], D[1], D[2], D[6]);
  and and_1 (and_1_out, D[6], T[5]);
  and and_2 (and_2_out, T[4], or_1_out);
  Multiplexer #(.width(16), .enable("false")) multiplexer_1 (
    .in0(Bus_IN), .in1(adder_1_out), .out(multiplexer_1_out), .sel(and_1_out));
  or or_2 (or_2_out, and_1_out, and_2_out);
  Register #(.width(16), .trigger("falling")) DR (
    .D(multiplexer_1_out), .en(or_2_out), .Q(Bus_OUT), .clk(Clock));  // open: clr
  Adder #(.width(16)) adder_1 (.a(16'h1), .b(Bus_OUT), .out(adder_1_out));  // open: cin, cout
endmodule

module OUTR (
  input  [15:0] Bus_IN,
  input  P,
  input  [11:0] B,
  input  Clock,
  output [3:0] out_5,
  output [3:0] out_6
);

  wire and_1_out;

  and and_1 (and_1_out, P, B[10]);
  Register OUTR (.D(Bus_IN[7:0]), .en(and_1_out), .Q({out_6, out_5}), .clk(Clock));  // open: clr
endmodule

module E (
  input  Clock,
  input  D,
  input  Clear,
  output Out,
  output Comp
);

  D_Flip_Flop E (.clk(Clock), .D(D), .Q(Out), .Qn(Comp), .reset(Clear));  // open: preset, en
endmodule

module IEN (
  input  IEN_J,
  input  Clock,
  input  IEN_K,
  output IEN_OUT
);

  J_K_Flip_Flop j_k_ff_1 (.J(IEN_J), .clk(Clock), .K(IEN_K), .Q(IEN_OUT));  // open: Qn, preset, en, reset
endmodule

module FGI (
  input  FGI_J,
  input  Clock,
  input  FGI_K,
  output FGI_OUT
);

  J_K_Flip_Flop j_k_ff_1 (.J(FGI_J), .clk(Clock), .K(FGI_K), .Q(FGI_OUT));  // open: Qn, preset, en, reset
endmodule

module FGO (
  input  FGO_J,
  input  Clock,
  input  FGO_K,
  output FGO_OUT
);

  J_K_Flip_Flop j_k_ff_1 (.J(FGO_J), .clk(Clock), .K(FGO_K), .Q(FGO_OUT));  // open: Qn, preset, en, reset
endmodule

module R (
  input  [15:0] T,
  input  FGO,
  input  IEN,
  input  FGI,
  input  Clock,
  output OUT
);

  wire and_1_out, and_2_out, and_3_out, or_1_out;

  or or_1 (or_1_out, FGO, FGI);
  and and_1 (and_1_out, ~T[0], ~T[1], ~T[2]);  // AND_Gate
  and and_2 (and_2_out, T[2], OUT);
  and and_3 (and_3_out, IEN, or_1_out, and_1_out);
  J_K_Flip_Flop j_k_ff_1 (.J(and_3_out), .clk(Clock), .K(and_2_out), .Q(OUT));  // open: Qn, preset, en, reset
endmodule

module AC (
  input  r,
  input  [11:0] B,
  input  [15:0] ALU_IN,
  input  Clock,
  output [15:0] Bus_OUT
);

  wire and_1_out, and_2_out;
  wire [15:0] adder_1_out, multiplexer_1_out;

  Multiplexer #(.width(16), .enable("false")) multiplexer_1 (
    .in0(ALU_IN), .in1(adder_1_out), .out(multiplexer_1_out), .sel(and_1_out));
  and and_1 (and_1_out, r, B[5]);
  and and_2 (and_2_out, r, B[11]);
  Register #(.width(16), .trigger("falling")) AC (
    .D(multiplexer_1_out), .Q(Bus_OUT), .clk(Clock), .clr(and_2_out));  // open: en
  Adder #(.width(16)) adder_1 (.a(16'h1), .b(Bus_OUT), .out(adder_1_out));  // open: cin, cout
endmodule

module ALU (
  input  [15:0] T,
  input  [7:0] D,
  input  [15:0] AC,
  input  [15:0] DR,
  input  [7:0] INPR,
  input  [11:0] B,
  input  r,
  input  E,
  input  p,
  output E_OUT,
  output [15:0] OUT
);

  wire ADD_out, and_3_out, and_4_out, and_5_out, AND_out, COM_out, Cout, DR_out, INPR_out, not_1_out,
       or_1_out, SHL_out, SHR_out;
  wire [2:0] Selector;
  wire [15:0] adder_1_out, and_2_out, not_2_out, shifter_1_out, shifter_2_out;

  and AND (AND_out, D[0], T[5]);
  and ADD (ADD_out, D[1], T[5]);
  and u_DR (DR_out, D[2], T[5]);
  and u_INPR (INPR_out, p, B[11]);
  and COM (COM_out, r, B[9]);
  and SHL (SHL_out, r, B[6]);
  and SHR (SHR_out, r, B[7]);
  Shifter #(.width(16), .shift("lr")) shifter_1 (.in(AC), .\dist (4'b0001), .out(shifter_1_out));
  or or_1 (or_1_out, SHR_out, SHL_out, COM_out, INPR_out, DR_out, ADD_out, AND_out);
  Shifter #(.width(16)) shifter_2 (.in(AC), .\dist (4'b0001), .out(shifter_2_out));
  not not_1 (not_1_out, or_1_out);
  Priority_Encoder priority_encoder_1 (
    .in0(not_1_out), .in1(AND_out), .in2(ADD_out), .in3(DR_out), .in4(INPR_out), .in5(COM_out),
    .in6(SHL_out), .in7(SHR_out), .out(Selector));  // open: en_in, gs, en_out
  assign not_2_out = ~AC;  // NOT_Gate not_2, 16 bits wide
  assign and_2_out = AC & DR;  // AND_Gate and_2, 16 bits wide
  Adder #(.width(16)) adder_1 (.a(DR), .b(AC), .out(adder_1_out), .cout(Cout));  // open: cin
  Multiplexer #(.select(3), .width(16), .enable("false")) multiplexer_1 (
    .in0(AC), .in1(and_2_out), .in2(adder_1_out), .in3(DR), .in4({{8{1'b0}}, INPR}), .in5(not_2_out),
    .in6({shifter_2_out[15:1], E}), .in7({E, shifter_1_out[14:0]}), .out(OUT), .sel(Selector));
  and and_3 (and_3_out, Cout, ~Selector[0], Selector[1], Selector[2]);  // AND_Gate
  and and_4 (and_4_out, AC[0], ~Selector[0], ~Selector[1], Selector[2]);  // AND_Gate
  and and_5 (and_5_out, AC[15], Selector[0], Selector[1], ~Selector[2]);  // AND_Gate
  or or_2 (E_OUT, and_3_out, and_4_out, and_5_out);
endmodule

module SC (
  input  [15:0] T,
  input  [7:0] D,
  input  R,
  input  Clock,
  input  I,
  output [15:0] T_2
);

  wire and_1_out, and_2_out, and_3_out, and_4_out, and_5_out, and_6_out, and_7_out, and_8_out, D4_out,
       or_1_out, or_2_out, T4_out, T6_out;
  wire [3:0] adder_1_out, register_1_q;

  and and_1 (and_1_out, D[2], T[6]);
  and and_2 (and_2_out, D[1], T[6]);
  and T4 (T4_out, D[3], T[5]);
  and D4 (D4_out, D[4], T[5]);
  and and_3 (and_3_out, D[0], T[6]);
  and and_4 (and_4_out, D[5], T[6]);
  and and_5 (and_5_out, R, T[3]);
  and T6 (T6_out, D[6], T[7]);
  and and_6 (and_6_out, D[7], ~I, T[4]);  // AND_Gate
  and and_7 (and_7_out, D[7], I, T[4]);
  or or_1 (or_1_out, and_5_out, and_3_out, and_2_out, and_1_out, T4_out, D4_out, and_4_out, T6_out, and_6_out, and_7_out);
  Adder #(.width(4)) adder_1 (.a(4'b0001), .b(register_1_q), .out(adder_1_out));  // open: cin, cout
  Register #(.width(4)) register_1 (.D(adder_1_out), .Q(register_1_q), .clk(Clock), .clr(or_2_out));  // open: en
  or or_2 (or_2_out, or_1_out, and_8_out);
  and and_8 (and_8_out, register_1_q[3], register_1_q[2], register_1_q[1], register_1_q[0]);
  Decoder #(.select(4)) decoder_1 (
    .out0(T_2[0]), .out1(T_2[1]), .out2(T_2[2]), .out3(T_2[3]), .out4(T_2[4]), .out5(T_2[5]), .out6(T_2[6]),
    .out7(T_2[7]), .out8(T_2[8]), .out9(T_2[9]), .out10(T_2[10]), .out11(T_2[11]), .out12(T_2[12]),
    .out13(T_2[13]), .out14(T_2[14]), .out15(T_2[15]), .sel(register_1_q));  // open: en
endmodule

// Bus Selector
module BUS_Selector (
  input  [7:0] D,
  input  [15:0] T,
  input  R,
  input  p,
  input  [11:0] B,
  input  I,
  output [2:0] Bus_Select
);

  wire AC_out, and_1_out, and_2_out, and_3_out, and_4_out, and_5_out, and_6_out, and_7_out, and_8_out,
       and_9_out, and_10_out, and_11_out, AR_out, DR_out, IR_out, MR_out, or_1_out, PC_out, TR_out;

  and and_1 (and_1_out, D[2], T[5]);
  and and_2 (and_2_out, D[6], T[6]);
  and and_3 (and_3_out, D[5], T[5]);
  and and_4 (and_4_out, D[5], T[4]);
  and and_5 (and_5_out, p, B[10]);
  and and_6 (and_6_out, ~R, T[1]);  // AND_Gate
  or or_1 (or_1_out, D[0], D[1], D[2], D[6]);
  and and_7 (and_7_out, D[4], T[4]);
  or AR (AR_out, and_7_out, and_3_out);
  or PC (PC_out, T[0], and_4_out);
  or DR (DR_out, and_2_out, and_1_out);
  and and_8 (and_8_out, D[3], T[4]);
  or AC (AC_out, and_8_out, and_5_out);
  and IR (IR_out, ~R, T[2]);  // AND_Gate
  and TR (TR_out, R, T[1]);
  and and_9 (and_9_out, ~D[7], I, T[3]);  // AND_Gate
  and and_10 (and_10_out, T[4], or_1_out);
  or MR (MR_out, and_9_out, and_6_out, and_10_out);
  and and_11 (and_11_out, ~AR_out, ~PC_out, ~DR_out, ~AC_out, ~IR_out, ~TR_out, ~MR_out);  // AND_Gate
  Priority_Encoder priority_encoder_1 (
    .in0(and_11_out), .in1(AR_out), .in2(PC_out), .in3(DR_out), .in4(AC_out), .in5(IR_out), .in6(TR_out),
    .in7(MR_out), .out(Bus_Select));  // open: en_in, gs, en_out
endmodule

module Memory_Controler (
  input  R,
  input  [7:0] D,
  input  [15:0] T,
  output MR_Load
);

  wire and_1_out, and_2_out, and_3_out, and_4_out, or_1_out;

  and and_1 (and_1_out, R, T[1]);
  and and_2 (and_2_out, D[3], T[4]);
  and and_3 (and_3_out, D[6], T[6]);
  and and_4 (and_4_out, D[5], T[4]);
  or or_1 (or_1_out, and_1_out, and_2_out, and_3_out, and_4_out);
  not not_1 (MR_Load, or_1_out);
endmodule

module FGI_O_IEN_Controler (
  input  [15:0] T,
  input  [11:0] B,
  input  p,
  input  R,
  input  Clock,
  input  [7:0] INPR,
  output FGI_J,
  output Clock_2,
  output FGI_K,
  output FGO_J,
  output Clock_3,
  output FGO_K,
  output IEN_J,
  output Clock_4,
  output IEN_K
);

  wire and_1_out, and_2_out;

  and and_1 (and_1_out, B[6], p);
  and and_2 (and_2_out, R, T[2]);
  or or_1 (FGI_J, INPR[0], INPR[1], INPR[2], INPR[3], INPR[4], INPR[5], INPR[6], INPR[7]);
  and and_3 (FGI_K, B[11], p);
  and and_4 (FGO_K, B[10], p);
  and and_5 (IEN_J, B[7], p);
  or or_2 (IEN_K, and_1_out, and_2_out);

  assign Clock_2 = Clock;
  assign Clock_3 = Clock;
  assign Clock_4 = Clock;
  assign FGO_J = T[0];
endmodule

module E_Controler (
  input  [15:0] T,
  input  [11:0] B,
  input  [7:0] D,
  input  r,
  input  IN,
  input  Comp,
  output D_2,
  output Clear
);

  wire and_1_out, and_2_out, and_3_out, and_4_out, and_5_out, or_1_out;

  and and_1 (and_1_out, r, B[7]);
  and and_2 (and_2_out, r, B[6]);
  and and_3 (and_3_out, D[1], T[5]);
  or or_1 (or_1_out, and_1_out, and_2_out, and_3_out);
  and and_4 (and_4_out, r, B[8], Comp);
  and and_5 (and_5_out, or_1_out, IN);
  or or_2 (D_2, and_4_out, and_5_out);
  and and_6 (Clear, r, B[10]);
endmodule
